# Fritzing sketch BaseSensor (saved by Fritzing 0.9.10b)

parts:
  Mod1 = Raspberry Pi Pico
  U1 = RFM69 [part_number=FRM69]
  Mod2 = KY-004 Key Switch Module [package="Breakout board"]

nets:
  N1: Mod1.pin_1, Mod2.S
  GND1: Mod1.pin_3, Mod1.pin_18, Mod1.pin_33, U1.GND1, U1.GND2, U1.NC, Mod2.-
  N2: Mod1.pin_12, U1.D00
  N3: Mod1.pin_14, U1.RST
  N4: Mod1.pin_15, U1.MOSI
  N5: Mod1.pin_16, U1.MISO
  N6: Mod1.pin_17, U1.NSS
  N7: Mod1.pin_19, U1.SCK
  3V3: Mod1.pin_36, U1.3V3, Mod2.Vin

notes:
  3.3V
  5V

custom parts:
  Raspberry Pi Pico: Raspberry Pi Pico. Based around the RP2040 microcontroller the Pico is a low cost microcontroller device bringing Raspberry Pi quality, cost, and easy of use to the microcontroller space. Jan 2021, Split part in to two versions: tht (this one) and SMD. This one will drill holes for a .1 in header in pcb to allow plugging in the module as well as providing pads to solder the module to the top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
  RFM69: ISM TRANSCEIVER MODULE v1.1
  KY-004 Key Switch Module: Arduino Key Switch Module Keyes KY-004 is a push button that will output a high signal when pressed.
