# Fritzing sketch DoorSensor (saved by Fritzing 0.9.10b)

parts:
  S4 = Magnetic Door Switch [package=reed_switch_plastic]
  Part2 = Adafruit Feather M0 RFM69 [part_number="Adafruit #3176 or #3177"]
  ANT2 = Antenna
  Mod2 = KY-004 Key Switch Module [package="Breakout board"]

nets:
  N1: S4.1, Part2.D12
  +3V3: S4.2, Part2.+3V3, Mod2.Vin
  N2: Part2.GND, Mod2.-
  N3: Part2.ANT, ANT2.antenna_lead
  N4: Part2.D13, Mod2.S

custom parts:
  Adafruit Feather M0 RFM69: This is the Adafruit Feather M0 RFM69 Packet Radio - our take on an microcontroller with a RFM69HCW packet radio transceiver plus built in USB and battery charging. Its an Adafruit Feather M0 with a 433MHz or 900MHz radio module cooked in! We have other boards in the Feather family, check'em out here. At the Feather M0's heart is an ATSAMD21G18 ARM Cortex M0 processor, clocked at 48 MHz and at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
  KY-004 Key Switch Module: Arduino Key Switch Module Keyes KY-004 is a push button that will output a high signal when pressed.
