# Fritzing sketch Test_water_sensor (saved by Fritzing 0.9.10b)

parts:
  Part2 = Adafruit Feather M0 RFM69 [part_number="Adafruit #3176 or #3177"]
  ANT2 = Antenna
  Mod2 = KY-004 Key Switch Module [package="Breakout board"]
  Water_Level_Sensor1 = Water Level Sensor

nets:
  GND: Part2.GND, Mod2.-, Water_Level_Sensor1.GND
  +3V3: Part2.+3V3, Mod2.Vin, Water_Level_Sensor1.VCC
  N1: Part2.ANT, ANT2.antenna_lead
  N2: Part2.D13, Mod2.S
  N3: Part2.D12, Water_Level_Sensor1.SIG

custom parts:
  Adafruit Feather M0 RFM69: This is the Adafruit Feather M0 RFM69 Packet Radio - our take on an microcontroller with a RFM69HCW packet radio transceiver plus built in USB and battery charging. Its an Adafruit Feather M0 with a 433MHz or 900MHz radio module cooked in! We have other boards in the Feather family, check'em out here. At the Feather M0's heart is an ATSAMD21G18 ARM Cortex M0 processor, clocked at 48 MHz and at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
  KY-004 Key Switch Module: Arduino Key Switch Module Keyes KY-004 is a push button that will output a high signal when pressed.
  Water Level Sensor: A water level sensor. This sensor operates at 3V to 5V. The Sig (signal) pin outputs an analogue signal that is in proportion to the amount of water in contact with the sensor.
